# Fritzing sketch LCD-Ethernet-Nano-to-W204B-NLW (saved by Fritzing 0.3.16b)

parts:
  Arduino_Nano = Arduino Nano v2.3
  LCD = LCD screen
  R1 = Rotary Potentiometer (Large) [package=THT]
  EthernetShield = Arduino
  10_Ohm = Resistor [resistance=10 package=THT]

nets:
  N1: Arduino_Nano.D1TX, EthernetShield.D1TX
  N2: Arduino_Nano.D0RX, EthernetShield.D0RX
  GND: Arduino_Nano.GND, LCD.VSS, LCD.LED-, R1.wiper, EthernetShield.GND
  N3: Arduino_Nano.D2, LCD.DB7
  N4: Arduino_Nano.D3, LCD.DB6
  N5: Arduino_Nano.D4, LCD.DB5
  N6: Arduino_Nano.D5, LCD.DB4
  N7: Arduino_Nano.D6, LCD.E
  N8: Arduino_Nano.D7, LCD.R/W
  N9: Arduino_Nano.D8, LCD.RS
  N10: Arduino_Nano.D9, EthernetShield.RST
  N11: Arduino_Nano.D10, EthernetShield.D10
  N12: Arduino_Nano.D11, EthernetShield.D11
  N13: Arduino_Nano.D12, EthernetShield.D12
  N14: Arduino_Nano.D13, EthernetShield.D13
  N15: Arduino_Nano.AREF, EthernetShield.aref
  5V: Arduino_Nano.+5V, LCD.VDD, R1.leg1, EthernetShield.+5V, 10_Ohm.Pin_0
  N16: LCD.V0, R1.leg2
  N17: LCD.LED+, 10_Ohm.Pin_1
